# Fritzing sketch Touch + WS2813 Circuit (saved by Fritzing 0.9.1b)

parts:
  Part1 = Adafruit Proto Shield R3 [part_number="Adafruit #2077"]
  R1 = Resistor [tolerance=±5% resistance=220 package=THT]
  NEOPIXEL1 = Neopixel Strip -- Black (60/m)
  BATT1 = LiPoly Battery (1300mAh)

nets:
  GND: Part1.GND, NEOPIXEL1.GND, BATT1.negative
  N1: Part1.D2, R1.Pin_1
  N2: Part1.D4, R1.Pin_0
  N3: Part1.D10, NEOPIXEL1.DI
  +5V: Part1.+5V, NEOPIXEL1.+5V, BATT1.positive

custom parts:
  Adafruit Proto Shield R3: This prototyping shield is the best out there (well, we think so, at least), and now is even better with Version R3 - updated for the most compatibility with just about all the Arduinos! It works with UNO, Mega, Leonardo, NG, Diecimila, Duemilanove, and compatible Arduinos. Yun's and Arduino Ethernets have a chunky Ethernet jack that gets in the way of stacking, you can use the stacking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
  Neopixel Strip -- Black (60/m): Neopixel Strip, Black, 60 pixels per meter.
  LiPoly Battery (1300mAh): Lithium Ion Polymer Battery (1300mAh)
